// Logisim project Practica4.circ as structural Verilog
module XOR (
  input  P,
  input  Q,
  output P_XOR_Q
);

  wire and_1_out, and_2_out, not_1_out, not_2_out;

  not not_1 (not_1_out, P);
  not not_2 (not_2_out, Q);
  and and_1 (and_1_out, not_1_out, Q);
  and and_2 (and_2_out, P, not_2_out);
  or or_1 (P_XOR_Q, and_1_out, and_2_out);

  // Notes on the sheet:
  //   Compuerta XOR
endmodule

// ALU
module ALU_1_bit_suma (
  input  Ci,
  input  [1:0] Op,
  input  A,
  input  B,
  output A_Op_B,
  output Ci_1
);

  wire and_1_out, and_2_out, and_3_out, or_1_out, xor_1_p_xor_q, xor_2_p_xor_q;

  and and_1 (and_1_out, B, A);
  and and_2 (and_2_out, A, B);
  or or_1 (or_1_out, A, B);
  XOR xor_1 (.P(A), .Q(B), .P_XOR_Q(xor_1_p_xor_q));
  and and_3 (and_3_out, Ci, xor_1_p_xor_q);
  or or_2 (Ci_1, and_1_out, and_3_out);
  XOR xor_2 (.P(Ci), .Q(xor_1_p_xor_q), .P_XOR_Q(xor_2_p_xor_q));
  Multiplexer #(.select(2)) multiplexer_1 (
    .in0(and_2_out), .in1(or_1_out), .in2(xor_2_p_xor_q), .out(A_Op_B), .sel(Op));  // open: in3, en

  // Notes on the sheet:
  //   ALU de 1 bit suma
  //   Operaciones
  //   00- AND
  //   01-OR
  //   10-SUMA
endmodule

module ALU_8_bits_suma (
  input  C0,
  input  [1:0] Op,
  input  [7:0] A,
  input  [7:0] B,
  output [7:0] A_op_B,
  output Acarramiento
);

  wire alu_1_bit_suma_1_ci_1, alu_1_bit_suma_2_ci_1, alu_1_bit_suma_3_ci_1, alu_1_bit_suma_4_ci_1,
       alu_1_bit_suma_5_ci_1, alu_1_bit_suma_6_ci_1, alu_1_bit_suma_7_ci_1;

  ALU_1_bit_suma alu_1_bit_suma_1 (
    .A(A[0]), .B(B[0]), .A_Op_B(A_op_B[0]), .Ci(C0), .Op(Op), .Ci_1(alu_1_bit_suma_1_ci_1));
  ALU_1_bit_suma alu_1_bit_suma_2 (
    .A(A[1]), .B(B[1]), .A_Op_B(A_op_B[1]), .Ci(alu_1_bit_suma_1_ci_1), .Op(Op), .Ci_1(alu_1_bit_suma_2_ci_1));
  ALU_1_bit_suma alu_1_bit_suma_3 (
    .A(A[2]), .B(B[2]), .A_Op_B(A_op_B[2]), .Ci(alu_1_bit_suma_2_ci_1), .Op(Op), .Ci_1(alu_1_bit_suma_3_ci_1));
  ALU_1_bit_suma alu_1_bit_suma_4 (
    .A(A[3]), .B(B[3]), .A_Op_B(A_op_B[3]), .Ci(alu_1_bit_suma_3_ci_1), .Op(Op), .Ci_1(alu_1_bit_suma_4_ci_1));
  ALU_1_bit_suma alu_1_bit_suma_5 (
    .A(A[4]), .B(B[4]), .A_Op_B(A_op_B[4]), .Ci(alu_1_bit_suma_4_ci_1), .Op(Op), .Ci_1(alu_1_bit_suma_5_ci_1));
  ALU_1_bit_suma alu_1_bit_suma_6 (
    .A(A[5]), .B(B[5]), .A_Op_B(A_op_B[5]), .Ci(alu_1_bit_suma_5_ci_1), .Op(Op), .Ci_1(alu_1_bit_suma_6_ci_1));
  ALU_1_bit_suma alu_1_bit_suma_7 (
    .A(A[6]), .B(B[6]), .A_Op_B(A_op_B[6]), .Ci(alu_1_bit_suma_6_ci_1), .Op(Op), .Ci_1(alu_1_bit_suma_7_ci_1));
  ALU_1_bit_suma alu_1_bit_suma_8 (
    .A(A[7]), .B(B[7]), .A_Op_B(A_op_B[7]), .Ci(alu_1_bit_suma_7_ci_1), .Op(Op), .Ci_1(Acarramiento));

  // Notes on the sheet:
  //   ALU de 8 bits suma
  //   Operaciones
  //   00- AND
  //   01-OR
  //   10-SUMA
endmodule

// RESTA
module ALU_1_bit_resta (
  input  Operacion,
  input  A,
  input  B,
  output A_op_B,
  output Acarreo,
  output Overflow
);

  wire and_1_out, and_2_out, not_1_out, not_2_out, not_3_out, xor_1_p_xor_q;

  XOR xor_1 (.P(Operacion), .Q(B), .P_XOR_Q(xor_1_p_xor_q));
  not not_1 (not_1_out, xor_1_p_xor_q);
  not not_2 (not_2_out, A);
  ALU_1_bit_suma alu_1_bit_suma_1 (
    .A(A), .B(xor_1_p_xor_q), .A_Op_B(A_op_B), .Ci(Operacion), .Op(2'b10), .Ci_1(Acarreo));
  not not_3 (not_3_out, A_op_B);
  and and_1 (and_1_out, A_op_B, not_2_out, not_1_out);
  and and_2 (and_2_out, xor_1_p_xor_q, not_3_out, A);
  or or_1 (Overflow, and_1_out, and_2_out);

  // Notes on the sheet:
  //   ALU de 1 bit de suma y resta
  //   Operaciones
  //   0-SUMA
  //   1-RESTA
endmodule

// ALU -
module ALU_8_bits_igualdad (
  input  [7:0] A,
  input  [7:0] B,
  output [7:0] A_op_B,
  output out_4,
  output out_5
);

  wire [7:0] undriven;

  ALU_1_bit_resta alu_1_bit_resta_1 (
    .A(undriven[0]), .B(B[0]), .A_op_B(A_op_B[0]), .Acarreo(out_4), .Overflow(out_5), .Operacion(1'b1));
  ALU_1_bit_resta alu_1_bit_resta_2 (
    .A(undriven[1]), .B(B[1]), .A_op_B(A_op_B[1]), .Acarreo(out_5), .Overflow(out_4), .Operacion(1'b1));
  ALU_1_bit_resta alu_1_bit_resta_3 (
    .A(undriven[2]), .B(B[2]), .A_op_B(A_op_B[2]), .Acarreo(out_5), .Overflow(out_4), .Operacion(1'b1));
  ALU_1_bit_resta alu_1_bit_resta_4 (
    .A(undriven[3]), .B(B[3]), .A_op_B(A_op_B[3]), .Acarreo(out_5), .Overflow(out_4), .Operacion(1'b1));
  ALU_1_bit_resta alu_1_bit_resta_5 (
    .A(undriven[4]), .B(B[4]), .A_op_B(A_op_B[4]), .Acarreo(out_5), .Overflow(out_4), .Operacion(1'b1));
  ALU_1_bit_resta alu_1_bit_resta_6 (
    .A(undriven[5]), .B(B[5]), .A_op_B(A_op_B[5]), .Acarreo(out_5), .Overflow(out_4), .Operacion(1'b1));
  ALU_1_bit_resta alu_1_bit_resta_7 (
    .A(undriven[6]), .B(B[6]), .A_op_B(A_op_B[6]), .Acarreo(out_5), .Overflow(out_4), .Operacion(1'b1));
  ALU_1_bit_resta alu_1_bit_resta_8 (
    .A(undriven[7]), .B(B[7]), .A_op_B(A_op_B[7]), .Acarreo(out_5), .Overflow(out_4), .Operacion(1'b1));

  // Notes on the sheet:
  //   ALU de 8 bits igualdad
  //   Significados
  //   00000000-Son iguales
  //   Cualquier otra cosa- Son diferentes
endmodule

module ALU_1_bit_NOR (
  input  A,
  input  B,
  output A_NOR_B
);

  wire and_1_out;

  and and_1 (and_1_out, A, B);
  not not_1 (A_NOR_B, and_1_out);

  // Notes on the sheet:
  //   ALU de 1 bit NOR
endmodule

module ALU_8_bits_NOR (
  input  [7:0] A,
  input  [7:0] B,
  output [7:0] A_op_B,
  output Acarramiento
);

  wire alu_1_bit_suma_1_a_op_b, alu_1_bit_suma_1_ci_1, alu_1_bit_suma_2_a_op_b, alu_1_bit_suma_2_ci_1,
       alu_1_bit_suma_3_a_op_b, alu_1_bit_suma_3_ci_1, alu_1_bit_suma_4_a_op_b, alu_1_bit_suma_4_ci_1,
       alu_1_bit_suma_5_a_op_b, alu_1_bit_suma_5_ci_1, alu_1_bit_suma_6_a_op_b, alu_1_bit_suma_6_ci_1,
       alu_1_bit_suma_7_a_op_b, alu_1_bit_suma_7_ci_1, alu_1_bit_suma_8_a_op_b;

  ALU_1_bit_suma alu_1_bit_suma_1 (
    .A(A[0]), .B(B[0]), .A_Op_B(alu_1_bit_suma_1_a_op_b), .Ci(1'b0), .Op(2'b00), .Ci_1(alu_1_bit_suma_1_ci_1));
  ALU_1_bit_suma alu_1_bit_suma_2 (
    .A(A[1]), .B(B[1]), .A_Op_B(alu_1_bit_suma_2_a_op_b), .Ci(alu_1_bit_suma_1_ci_1), .Op(2'b00),
    .Ci_1(alu_1_bit_suma_2_ci_1));
  ALU_1_bit_suma alu_1_bit_suma_3 (
    .A(A[2]), .B(B[2]), .A_Op_B(alu_1_bit_suma_3_a_op_b), .Ci(alu_1_bit_suma_2_ci_1), .Op(2'b00),
    .Ci_1(alu_1_bit_suma_3_ci_1));
  ALU_1_bit_suma alu_1_bit_suma_4 (
    .A(A[3]), .B(B[3]), .A_Op_B(alu_1_bit_suma_4_a_op_b), .Ci(alu_1_bit_suma_3_ci_1), .Op(2'b00),
    .Ci_1(alu_1_bit_suma_4_ci_1));
  ALU_1_bit_suma alu_1_bit_suma_5 (
    .A(A[4]), .B(B[4]), .A_Op_B(alu_1_bit_suma_5_a_op_b), .Ci(alu_1_bit_suma_4_ci_1), .Op(2'b00),
    .Ci_1(alu_1_bit_suma_5_ci_1));
  ALU_1_bit_suma alu_1_bit_suma_6 (
    .A(A[5]), .B(B[5]), .A_Op_B(alu_1_bit_suma_6_a_op_b), .Ci(alu_1_bit_suma_5_ci_1), .Op(2'b00),
    .Ci_1(alu_1_bit_suma_6_ci_1));
  ALU_1_bit_suma alu_1_bit_suma_7 (
    .A(A[6]), .B(B[6]), .A_Op_B(alu_1_bit_suma_7_a_op_b), .Ci(alu_1_bit_suma_6_ci_1), .Op(2'b00),
    .Ci_1(alu_1_bit_suma_7_ci_1));
  ALU_1_bit_suma alu_1_bit_suma_8 (
    .A(A[7]), .B(B[7]), .A_Op_B(alu_1_bit_suma_8_a_op_b), .Ci(alu_1_bit_suma_7_ci_1), .Op(2'b00),
    .Ci_1(Acarramiento));
  not not_1 (A_op_B[1], alu_1_bit_suma_2_a_op_b);
  not not_2 (A_op_B[2], alu_1_bit_suma_3_a_op_b);
  not not_3 (A_op_B[3], alu_1_bit_suma_4_a_op_b);
  not not_4 (A_op_B[4], alu_1_bit_suma_5_a_op_b);
  not not_5 (A_op_B[5], alu_1_bit_suma_6_a_op_b);
  not not_6 (A_op_B[6], alu_1_bit_suma_7_a_op_b);
  not not_7 (A_op_B[7], alu_1_bit_suma_8_a_op_b);
  not not_8 (A_op_B[0], alu_1_bit_suma_1_a_op_b);

  // Notes on the sheet:
  //   ALU de 8 bits suma
  //   Operaciones
  //   00- AND
  //   01-OR
  //   10-SUMA
endmodule
